# Fritzing sketch circuito_projeto (saved by Fritzing 1.0.2b)

parts:
  Componente1 = Arduino Mega 2560 (Rev3)
  IR1 = TSOP312.., 314.. [package=THT]
  A1 = Electropeak 2.4in LCD
  Componente4 = RFID-RC522-v2
  LED2 = smd LED [color="Red (633nm)" package="0805 [SMD]"]

nets:
  N1: Componente1.A0, A1.Pin_7
  N2: Componente1.A1, A1.Pin_8
  N3: Componente1.A2, A1.Pin_9
  N4: Componente1.A3, A1.Pin_10
  N5: Componente1.A4, A1.Pin_11
  N6: Componente1.A5, A1.Pin_12
  N7: Componente1.D21/SCL, LED2.cathode
  N8: Componente1.D20/SDA, IR1.Data
  N9: Componente1.AREF, A1.Pin_28
  GND: Componente1.GND, IR1.GND, A1.Pin_4, A1.Pin_5, A1.Pin_27, Componente4.GND, LED2.anode
  N10: Componente1.D13_PWM, A1.Pin_26
  N11: Componente1.D12_PWM, A1.Pin_25
  N12: Componente1.D11_PWM, A1.Pin_24
  N13: Componente1.D10_PWM, A1.Pin_23
  N14: Componente1.D9_PWM, A1.Pin_22
  N15: Componente1.D8_PWM, A1.Pin_21
  N16: Componente1.RESET, A1.Pin_1
  3V3: Componente1.3V3, IR1.Vs, A1.Pin_2, Componente4.3.3V
  N17: Componente1.5V, A1.Pin_3
  N18: Componente1.VIN, A1.Pin_6
  N19: Componente1.D0_RX0, A1.Pin_13
  N20: Componente1.D1_TX0, A1.Pin_14
  N21: Componente1.D2_PWM, A1.Pin_15
  N22: Componente1.D3_PWM, A1.Pin_16
  N23: Componente1.D4_PWM, A1.Pin_17
  N24: Componente1.D5_PWM, A1.Pin_18
  N25: Componente1.D6_PWM, A1.Pin_19
  N26: Componente1.D7_PWM, A1.Pin_20
  N27: Componente1.D23, Componente4.RST
  N28: Componente1.D50, Componente4.MISO
  N29: Componente1.D51, Componente4.MOSI
  N30: Componente1.D52, Componente4.SCK
  N31: Componente1.D53, Componente4.SDA

custom parts:
  Electropeak 2.4in LCD: 2.4 inch Touch TFT LCD Display Shield for Arduino UNO/Mega.
  RFID-RC522-v2: A simple China made RFID-RC522 Reader; do check the pin labels, as this is a MFRC522 based clone.
